# Fritzing sketch Conexion (saved by Fritzing 0.9.1b)

parts:
  Parte1 = Arduino Mega 2560 (Rev3)
  Parte2 = Arduino Mega 2560 (Rev3)
  Parte4 = Compass Module - HMC6352
  Parte3 = Arduino Prototyping Shield

nets:
  N1: Parte1.D21/SCL, Parte4.SCL
  N2: Parte1.D20/SDA, Parte4.SDA
  5V: Parte1.5V, Parte4.VCC
  GND: Parte1.GND, Parte4.GND, Parte3.GND
  N3: Parte1.D2_PWM, Parte2.D22

notes:
  Imagen no representativa, este shield conecta con el brazo
  Representa el VL6180x
  Un GND viaja en twisted pair con SDA y el otro con SCL, para minimizar el ruido
  Conectar los GND para poder comunicar los arduinos
